# Fritzing sketch 7204baPotansiometr (saved by Fritzing 0.9.4)
breadboards: 1

parts:
  VCC3 = Battery
  U1 = 74HC04_HEX_INVERTER [package=dil14]
  R2 = Rotary Potentiometer (Small) [maximum_resistance=100kΩ package=THT]

nets:
  N1: VCC3.-, U1.GND, R2.leg2
  N2: VCC3.+, U1.VCC, R2.leg1
  N3: U1.1A, R2.wiper

notes:
  Oscilloscope
