# Fritzing sketch ManbaTaqzieMoteqaier (saved by Fritzing 0.9.4)
breadboards: 1

parts:
  VCC2 = Battery
  R1 = Rotary Potentiometer (Small) [maximum_resistance=100kΩ package=THT]

nets:
  N1: VCC2.-, R1.leg2
  N2: VCC2.+, R1.leg1

notes:
  Output
