# Fritzing sketch TurnLEDOn (saved by Fritzing 0.9.4)
breadboards: 1

parts:
  R1 = Resistor [tolerance=±5% resistance=330 package=THT]
  LED1 = smd LED [color="Red (633nm)" package="1206 [SMD]"]
  VCC1 = Battery

nets:
  N1: R1.Pin_0, VCC1.-
  N2: R1.Pin_1, LED1.cathode
  N3: LED1.anode, VCC1.+
