# Fritzing sketch 10TimesNAND (saved by Fritzing 0.9.4)
breadboards: 2

parts:
  U1 = SN74LS20N [package="DIP14 [THT]"]
  VCC4 = 4 x AAA Battery Mount
  R1 = Resistor [tolerance=±5% resistance=1k package=THT]
  R2 = Rotary Potentiometer (Small) [maximum_resistance=100kΩ package=THT]
  U2 = SN74LS20N [package="DIP14 [THT]"]
  U3 = SN74LS20N [package="DIP14 [THT]"]
  U4 = SN74LS20N [package="DIP14 [THT]"]

nets:
  N1: U1.1A, R1.Pin_1
  N2: U1.1B, R2.wiper
  N3: U1.NC#2, U2.1A, U2.1B
  GND: U1.GND, VCC4.-, R2.leg2, U2.GND, U3.GND, U4.GND
  VCC: U1.VCC, VCC4.+, R1.Pin_0, R2.leg1, U2.VCC, U3.VCC, U4.VCC
  N4: U2.NC#2, U2.1C, U2.1D
  N5: U2.1Y, U2.2C, U2.2D
  N6: U2.2Y, U3.1A, U3.1B
  N7: U2.2A, U2.2B, U2.NC#10
  N8: U3.NC#2, U3.1C, U3.1D
  N9: U3.1Y, U3.2C, U3.2D
  N10: U3.2Y, U4.2C, U4.2D
  N11: U3.2A, U3.2B, U3.NC#10
  N12: U4.2A, U4.2B, U4.NC#10

notes:
  Oscilloscope 2
  Oscilloscope 1
