# Fritzing sketch 10Not (saved by Fritzing 0.9.4)
breadboards: 2

parts:
  U2 = 555 Timer [package="SO8 [SMD]"]  # not connected
  VCC2 = 4 x AAA Battery Mount
  C3 = Electrolytic Capacitor [capacitance=1nF package="200 mil [THT, electrolytic]"]
  R3 = Resistor [tolerance=±5% resistance=220 package="2010 [SMD]"]
  R4 = Resistor [tolerance=±5% resistance=220 package="2010 [SMD]"]
  C4 = Electrolytic Capacitor [capacitance=1nF package="100 mil [THT, electrolytic]"]
  U3 = 74HC04_HEX_INVERTER [package=dil14]
  U4 = 74HC04_HEX_INVERTER [package=dil14]

nets:
  GND: VCC2.-, C3.-, C4.+, U3.GND, U4.GND
  VCC: VCC2.+, R4.Pin_0, U3.VCC, U4.VCC
  N1: C3.+, R3.Pin_0
  N2: R3.Pin_1, R4.Pin_1
  N3: U3.1A, U3.5Y
  N4: U3.1Y, U3.2A
  N5: U3.2Y, U3.3A
  N6: U3.3Y, U4.6A
  N7: U3.5A, U3.6Y
  N8: U4.1A, U4.4Y
  N9: U4.1Y, U4.2A
  N10: U4.2Y, U4.3A
  N11: U4.4A, U4.5Y
  N12: U4.5A, U4.6Y

notes:
  Output
  Not Output
  Not Output With 10 Not Gates
