# Fritzing sketch PGozAz3 (saved by Fritzing 0.9.4)
breadboards: 1

parts:
  U1 = 555 Timer [package="SO8 [SMD]"]  # not connected
  VCC1 = 4 x AAA Battery Mount
  C1 = Electrolytic Capacitor [capacitance=100µF package="200 mil [THT, electrolytic]"]
  R1 = Resistor [tolerance=±5% resistance=220 package="2010 [SMD]"]
  R2 = Resistor [tolerance=±5% resistance=220 package="2010 [SMD]"]
  C2 = Electrolytic Capacitor [capacitance=1µF package="100 mil [THT, electrolytic]"]

nets:
  N1: VCC1.-, C2.+
  N2: VCC1.+, R2.Pin_0
  N3: C1.+, R1.Pin_0
  N4: R1.Pin_1, R2.Pin_1

notes:
  Output
