# Fritzing sketch VariableFrequency (saved by Fritzing 0.9.4)
breadboards: 1

parts:
  U2 = 555 Timer [package="SO8 [SMD]"]  # not connected
  VCC2 = 4 x AAA Battery Mount
  C3 = Electrolytic Capacitor [capacitance=1nF package="200 mil [THT, electrolytic]"]
  R3 = Resistor [tolerance=±5% resistance=220 package="2010 [SMD]"]
  R4 = Resistor [tolerance=±5% resistance=220 package="2010 [SMD]"]
  C4 = Electrolytic Capacitor [capacitance=1nF package="100 mil [THT, electrolytic]"]
  R5 = Rotary Potentiometer (Small) [maximum_resistance=100kΩ package=THT]

nets:
  N1: VCC2.-, C3.-, C4.+, R5.leg1
  N2: VCC2.+, R4.Pin_0, R5.leg2
  N3: C3.+, R3.Pin_0
  N4: R3.Pin_1, R4.Pin_1, R5.wiper

notes:
  Output
