# Fritzing sketch JohnsonCounter (saved by Fritzing 0.9.4)
breadboards: 1

parts:
  U2 = SN74LS32N [package="DIP14 [THT]"]
  VCC2 = 4 x AAA Battery Mount
  U3 = 74HC04_HEX_INVERTER [package=dil14]

nets:
  N1: U2.1A, U3.4Y
  GND: U2.2Y, U2.GND, VCC2.-, U3.GND
  N2: U2.3Y, U2.3A
  N3: U2.3B, U3.4A
  VCC: U2.Vcc, VCC2.+, U3.VCC

notes:
  Q0 Q1 Q2 Q3
  clock
