# Fritzing sketch ShiftRegisterWith7495 (saved by Fritzing 0.9.4)
breadboards: 1

parts:
  U1 = SN74LS32N [package="DIP14 [THT]"]
  R1 = Resistor [tolerance=±5% resistance=10k package="2010 [SMD]"]
  R2 = Resistor [tolerance=±5% resistance=10k package="2010 [SMD]"]
  S1 = Pushbutton [package="[SMD]"]
  S2 = Pushbutton [package="[SMD]"]
  VCC1 = 4 x AAA Battery Mount

nets:
  N1: U1.1A, R2.Pin_1, S1.Pin_3, S1.Pin_4
  N2: U1.2Y, R1.Pin_1, S2.Pin_3, S2.Pin_4
  N3: U1.GND, S1.Pin_1, S1.Pin_2, S2.Pin_1, S2.Pin_2, VCC1.-
  N4: U1.3Y, U1.3A
  N5: U1.Vcc, R1.Pin_0, R2.Pin_0, VCC1.+

notes:
  D0 D1 D2 D3
  clock
  Q0 Q1 Q2 Q3
